// Logisim project project.circ as structural Verilog: 13 circuits, main circuit main
module main (
);

  wire button_1_out, button_2_out, or_1_out;
  wire [31:0] counter_1_q, player_move_1__0, player_move_1__1, pull_resistor_1_node;

  Button button_1 (.out(button_1_out));
  Button button_2 (.out(button_2_out));
  Player_Move player_move_1 (.in_1(button_2_out), .in_2(button_1_out), ._0(player_move_1__0), ._1(player_move_1__1));
  or or_1 (or_1_out, button_1_out, button_2_out);
  // Probe on counter_1_q
  Counter #(.width(32), .max('h1f)) counter_1 (
    .load(button_1_out), .Q(counter_1_q), .clk(or_1_out));  // open: D, count, carry, clr
  Pull_Resistor pull_resistor_1 (.node(pull_resistor_1_node));
  DotMatrix #(.inputtype("row"), .matrixcols(32), .matrixrows(32)) dotmatrix_1 (
    .row0(pull_resistor_1_node), .row1(pull_resistor_1_node), .row2(pull_resistor_1_node),
    .row3(pull_resistor_1_node), .row4(pull_resistor_1_node), .row5(pull_resistor_1_node),
    .row6(pull_resistor_1_node), .row7(pull_resistor_1_node), .row8(pull_resistor_1_node),
    .row9(pull_resistor_1_node), .row10(pull_resistor_1_node), .row11(pull_resistor_1_node),
    .row12(pull_resistor_1_node), .row13(pull_resistor_1_node), .row14(pull_resistor_1_node),
    .row15(pull_resistor_1_node), .row16(pull_resistor_1_node), .row17(pull_resistor_1_node),
    .row18(pull_resistor_1_node), .row19(pull_resistor_1_node), .row20(pull_resistor_1_node),
    .row21(pull_resistor_1_node), .row22(pull_resistor_1_node), .row23(pull_resistor_1_node),
    .row24(pull_resistor_1_node), .row25(pull_resistor_1_node), .row26(pull_resistor_1_node),
    .row27(pull_resistor_1_node), .row28(pull_resistor_1_node), .row29(pull_resistor_1_node),
    .row30(player_move_1__1), .row31(player_move_1__0));
endmodule

module \трансформатор  (
  input  [4:0] in_1,
  output [31:0] out_2
);

  Comparator #(.width(5), .mode("unsigned")) comparator_1 (.a(in_1), .b({5{1'b0}}), .eq(out_2[0]));  // open: gt, lt
  Comparator #(.width(5), .mode("unsigned")) comparator_2 (.a(in_1), .b(5'b00001), .eq(out_2[1]));  // open: gt, lt
  Comparator #(.width(5), .mode("unsigned")) comparator_3 (.a(in_1), .b(5'b00010), .eq(out_2[2]));  // open: gt, lt
  Comparator #(.width(5), .mode("unsigned")) comparator_4 (.a(in_1), .b(5'b00011), .eq(out_2[3]));  // open: gt, lt
  Comparator #(.width(5), .mode("unsigned")) comparator_5 (.a(in_1), .b(5'b00100), .eq(out_2[4]));  // open: gt, lt
  Comparator #(.width(5), .mode("unsigned")) comparator_6 (.a(in_1), .b(5'b00101), .eq(out_2[5]));  // open: gt, lt
  Comparator #(.width(5), .mode("unsigned")) comparator_7 (.a(in_1), .b(5'b00110), .eq(out_2[6]));  // open: gt, lt
  Comparator #(.width(5), .mode("unsigned")) comparator_8 (.a(in_1), .b(5'b00111), .eq(out_2[7]));  // open: gt, lt
  Comparator #(.width(5), .mode("unsigned")) comparator_9 (.a(in_1), .b(5'b01000), .eq(out_2[8]));  // open: gt, lt
  Comparator #(.width(5), .mode("unsigned")) comparator_10 (.a(in_1), .b(5'b01001), .eq(out_2[9]));  // open: gt, lt
  Comparator #(.width(5), .mode("unsigned")) comparator_11 (.a(in_1), .b(5'b01010), .eq(out_2[10]));  // open: gt, lt
  Comparator #(.width(5), .mode("unsigned")) comparator_12 (.a(in_1), .b(5'b01011), .eq(out_2[11]));  // open: gt, lt
  Comparator #(.width(5), .mode("unsigned")) comparator_13 (.a(in_1), .b(5'b01100), .eq(out_2[12]));  // open: gt, lt
  Comparator #(.width(5), .mode("unsigned")) comparator_14 (.a(in_1), .b(5'b01101), .eq(out_2[13]));  // open: gt, lt
  Comparator #(.width(5), .mode("unsigned")) comparator_15 (.a(in_1), .b(5'b01110), .eq(out_2[14]));  // open: gt, lt
  Comparator #(.width(5), .mode("unsigned")) comparator_16 (.a(in_1), .b(5'b01111), .eq(out_2[15]));  // open: gt, lt
  Comparator #(.width(5), .mode("unsigned")) comparator_17 (.a(in_1), .b(5'b10000), .eq(out_2[16]));  // open: gt, lt
  Comparator #(.width(5), .mode("unsigned")) comparator_18 (.a(in_1), .b(5'b10001), .eq(out_2[17]));  // open: gt, lt
  Comparator #(.width(5), .mode("unsigned")) comparator_19 (.a(in_1), .b(5'b10010), .eq(out_2[18]));  // open: gt, lt
  Comparator #(.width(5), .mode("unsigned")) comparator_20 (.a(in_1), .b(5'b10011), .eq(out_2[19]));  // open: gt, lt
  Comparator #(.width(5), .mode("unsigned")) comparator_21 (.a(in_1), .b(5'b10100), .eq(out_2[20]));  // open: gt, lt
  Comparator #(.width(5), .mode("unsigned")) comparator_22 (.a(in_1), .b(5'b10101), .eq(out_2[21]));  // open: gt, lt
  Comparator #(.width(5), .mode("unsigned")) comparator_23 (.a(in_1), .b(5'b10110), .eq(out_2[22]));  // open: gt, lt
  Comparator #(.width(5), .mode("unsigned")) comparator_24 (.a(in_1), .b(5'b10111), .eq(out_2[23]));  // open: gt, lt
  Comparator #(.width(5), .mode("unsigned")) comparator_25 (.a(in_1), .b(5'b11000), .eq(out_2[24]));  // open: gt, lt
  Comparator #(.width(5), .mode("unsigned")) comparator_26 (.a(in_1), .b(5'b11001), .eq(out_2[25]));  // open: gt, lt
  Comparator #(.width(5), .mode("unsigned")) comparator_27 (.a(in_1), .b(5'b11010), .eq(out_2[26]));  // open: gt, lt
  Comparator #(.width(5), .mode("unsigned")) comparator_28 (.a(in_1), .b(5'b11011), .eq(out_2[27]));  // open: gt, lt
  Comparator #(.width(5), .mode("unsigned")) comparator_29 (.a(in_1), .b(5'b11100), .eq(out_2[28]));  // open: gt, lt
  Comparator #(.width(5), .mode("unsigned")) comparator_30 (.a(in_1), .b(5'b11101), .eq(out_2[29]));  // open: gt, lt
  Comparator #(.width(5), .mode("unsigned")) comparator_31 (.a(in_1), .b(5'b11110), .eq(out_2[30]));  // open: gt, lt
  Comparator #(.width(5), .mode("unsigned")) comparator_32 (.a(in_1), .b({5{1'b1}}), .eq(out_2[31]));  // open: gt, lt
endmodule

module \инкремент  (
  input  [4:0] X,
  output [4:0] R,
  output Cout
);

  wire [4:1] and_1_out;

  assign {Cout, and_1_out} = {and_1_out, 1'b1} & X;  // AND_Gate and_1, 5 bits wide
  assign R = X ^ {and_1_out, 1'b1};  // XOR_Gate xor_1, 5 bits wide
endmodule

module \декремент  (
  input  [7:0] X,
  output [7:0] R,
  output Cout
);

  wire [7:1] and_1_out;
  wire [7:7] and_1_out_2;

  assign R = ~(X ^ ~{and_1_out, 1'b1});  // XNOR_Gate xnor_1, 8 bits wide
  assign {and_1_out_2[7], and_1_out} = ~X & {and_1_out, 1'b1};  // AND_Gate and_1, 8 bits wide
  Multiplexer #(.disabled(0), .enable("false")) multiplexer_1 (
    .in0(1'b1), .in1(1'b0), .out(Cout), .sel(and_1_out_2[7]));
endmodule

module T_Block (
  input  A,
  input  B,
  input  C,
  output OUT
);

  or or_1 (OUT, A, B, C);
endmodule

module Player_Move (
  input  in_1,
  input  in_2,
  output [31:0] _0,
  output [31:0] _1
);

  wire or_1_out;
  wire [31:0] counter_1_q;

  T_Block t_block_1 (.A(_1[22]), .B(_1[24]), .C(_1[23]), .OUT(_0[23]));
  T_Block t_block_2 (.A(_1[21]), .B(_1[23]), .C(_1[22]), .OUT(_0[22]));
  T_Block t_block_3 (.A(_1[20]), .B(_1[22]), .C(_1[21]), .OUT(_0[21]));
  T_Block t_block_4 (.A(_1[19]), .B(_1[21]), .C(_1[20]), .OUT(_0[20]));
  T_Block t_block_5 (.A(_1[18]), .B(_1[20]), .C(_1[19]), .OUT(_0[19]));
  T_Block t_block_6 (.A(_1[17]), .B(_1[19]), .C(_1[18]), .OUT(_0[18]));
  T_Block t_block_7 (.A(_1[31]), .B(_1[1]), .C(_1[0]), .OUT(_0[0]));
  T_Block t_block_8 (.A(_1[16]), .B(_1[18]), .C(_1[17]), .OUT(_0[17]));
  T_Block t_block_9 (.A(_1[0]), .B(_1[2]), .C(_1[1]), .OUT(_0[1]));
  T_Block t_block_10 (.A(_1[1]), .B(_1[3]), .C(_1[2]), .OUT(_0[2]));
  T_Block t_block_11 (.A(_1[15]), .B(_1[17]), .C(_1[16]), .OUT(_0[16]));
  T_Block t_block_12 (.A(_1[2]), .B(_1[4]), .C(_1[3]), .OUT(_0[3]));
  T_Block t_block_13 (.A(_1[3]), .B(_1[5]), .C(_1[4]), .OUT(_0[4]));
  T_Block t_block_14 (.A(_1[14]), .B(_1[16]), .C(_1[15]), .OUT(_0[15]));
  T_Block t_block_15 (.A(_1[13]), .B(_1[15]), .C(_1[14]), .OUT(_0[14]));
  T_Block t_block_16 (.A(_1[12]), .B(_1[14]), .C(_1[13]), .OUT(_0[13]));
  T_Block t_block_17 (.A(_1[11]), .B(_1[13]), .C(_1[12]), .OUT(_0[12]));
  T_Block t_block_18 (.A(_1[10]), .B(_1[12]), .C(_1[11]), .OUT(_0[11]));
  T_Block t_block_19 (.A(_1[9]), .B(_1[11]), .C(_1[10]), .OUT(_0[10]));
  T_Block t_block_20 (.A(_1[8]), .B(_1[10]), .C(_1[9]), .OUT(_0[9]));
  T_Block t_block_21 (.A(_1[7]), .B(_1[9]), .C(_1[8]), .OUT(_0[8]));
  T_Block t_block_22 (.A(_1[4]), .B(_1[6]), .C(_1[5]), .OUT(_0[5]));
  T_Block t_block_23 (.A(_1[5]), .B(_1[6]), .C(_1[7]), .OUT(_0[6]));
  T_Block t_block_24 (.A(_1[25]), .B(_1[24]), .C(_1[23]), .OUT(_0[24]));
  T_Block t_block_25 (.A(_1[26]), .B(_1[25]), .C(_1[27]), .OUT(_0[26]));
  T_Block t_block_26 (.A(_1[27]), .B(_1[26]), .C(_1[28]), .OUT(_0[27]));
  T_Block t_block_27 (.A(_1[28]), .B(_1[27]), .C(_1[29]), .OUT(_0[28]));
  T_Block t_block_28 (.A(_1[31]), .B(_1[29]), .C(_1[30]), .OUT(_0[30]));
  T_Block t_block_29 (.A(_1[31]), .B(_1[30]), .C(_1[0]), .OUT(_0[31]));
  T_Block t_block_30 (.A(_1[25]), .B(_1[24]), .C(_1[26]), .OUT(_0[25]));
  T_Block t_block_31 (.A(_1[30]), .B(_1[29]), .C(_1[28]), .OUT(_0[29]));
  T_Block t_block_32 (.A(_1[6]), .B(_1[7]), .C(_1[8]), .OUT(_0[7]));
  // Probe on counter_1_q
  Counter #(.width(32), .max('h1f)) counter_1 (
    .load(in_1), .Q(counter_1_q), .clk(or_1_out));  // open: D, count, carry, clr
  or or_1 (or_1_out, in_1, in_2);
  \трансформатор  \u_трансформатор_1  (.in_1(counter_1_q[4:0]), .out_2(_1));
endmodule

module \богегознаетчто  (
);

  wire and_1_out, cdm_8_mark5_1_data_inst, cdm_8_mark5_1_mem_cycle, cdm_8_mark5_1_mem_read, code, data,
       not_1_out, write;
  wire [7:0] cdm_8_mark5_1_addr, cdm_8_mark5_1_data_out, cdm_8_mark5_1_r0, cdm_8_mark5_1_r1,
       cdm_8_mark5_1_r2, cdm_8_mark5_1_r3, controlled_buffer_1_out, controlled_buffer_2_out, register_1_q;

  CdM_8_mark5 cdm_8_mark5_1 (
    .addr(cdm_8_mark5_1_addr), .mem_read(cdm_8_mark5_1_mem_read), .mem_cycle(cdm_8_mark5_1_mem_cycle),
    .data_inst(cdm_8_mark5_1_data_inst), .data_out(cdm_8_mark5_1_data_out),
    .data_in(controlled_buffer_2_out), .r0(cdm_8_mark5_1_r0), .r1(cdm_8_mark5_1_r1), .r2(cdm_8_mark5_1_r2),
    .r3(cdm_8_mark5_1_r3));  // open: clock, PC, SP, PS, IAck, IRQ, vec, reset
  Decoder decoder_1 (.out0(code), .out1(data), .sel(cdm_8_mark5_1_data_inst), .en(cdm_8_mark5_1_mem_cycle));
  assign controlled_buffer_1_out = not_1_out ? cdm_8_mark5_1_data_out : 8'bz;  // Controlled_Buffer controlled_buffer_1
  not not_1 (not_1_out, cdm_8_mark5_1_mem_read);
  assign controlled_buffer_2_out = cdm_8_mark5_1_mem_read ? controlled_buffer_1_out : 8'bz;  // Controlled_Buffer controlled_buffer_2
  and and_1 (and_1_out, cdm_8_mark5_1_addr[0], cdm_8_mark5_1_addr[1], cdm_8_mark5_1_addr[2], cdm_8_mark5_1_addr[3], cdm_8_mark5_1_addr[4], cdm_8_mark5_1_addr[6], cdm_8_mark5_1_addr[7], data, write, write);
  Register register_1 (.D(cdm_8_mark5_1_data_out), .en(and_1_out), .Q(register_1_q));  // open: clk, clr
  RAM ram_1 (
    .addr(cdm_8_mark5_1_addr), .data(controlled_buffer_1_out), .sel(data), .ld(cdm_8_mark5_1_mem_read));  // open: clk, clr
  ROM #(.addrWidth(12)) rom_1 (
    .addr({register_1_q[3:0], controlled_buffer_1_out}), .data(controlled_buffer_1_out), .sel(code));
endmodule

module \монстр__т  (
  output [7:0] \_4строка ,
  output [7:0] \_3строка ,
  output [7:0] \_2строка ,
  output [7:0] \_1строка 
);


  assign \_1строка  = 8'h24;
  assign \_2строка  = 8'h5a;
  assign \_3строка  = 8'h18;
  assign \_4строка  = 8'h24;
endmodule

module \монстр__майн  (
  output [7:0] \_4строка ,
  output [7:0] \_3строка ,
  output [7:0] \_2строка ,
  output [7:0] \_1строка 
);


  assign \_1строка  = 8'h18;
  assign \_2строка  = 8'h24;
  assign \_3строка  = 8'h18;
  assign \_4строка  = 8'h24;
endmodule

module \стенка  (
  output [7:0] \_4строка ,
  output [7:0] \_3строка ,
  output [7:0] \_2строка ,
  output [7:0] \_1строка 
);


  assign \_1строка  = {8{1'b0}};
  assign \_2строка  = {8{1'b0}};
  assign \_3строка  = {8{1'b0}};
  assign \_4строка  = 8'h3c;
endmodule

module test (
);

  wire button_1_out, button_2_out, or_1_out;
  wire [31:0] counter_1_q, player_move_1__0, player_move_1__1, transpon_1__0, transpon_1__1, transpon_1__2,
       transpon_1__3, transpon_1__4, transpon_1__5, transpon_1__6, transpon_1__7, transpon_1__8,
       transpon_1__9, transpon_1__10, transpon_1__11, transpon_1__12, transpon_1__13, transpon_1__14,
       transpon_1__15, transpon_1__16, transpon_1__17, transpon_1__18, transpon_1__19, transpon_1__20,
       transpon_1__21, transpon_1__22, transpon_1__23, transpon_1__24, transpon_1__25, transpon_1__26,
       transpon_1__27, transpon_1__28, transpon_1__29, transpon_1__30, transpon_1__31;

  DotMatrix #(.matrixcols(32), .matrixrows(32)) dotmatrix_1 (
    .col0(player_move_1__0), .col1(player_move_1__1));  // open: col2, col3, col4, col5, col6, col7, col8, col9, col10, col11, col12, col13, col14, col15, col16, col17, col18, col19, col20, col21, col22, col23, col24, col25, col26, col27, col28, col29, col30, col31
  Button button_1 (.out(button_1_out));
  Button button_2 (.out(button_2_out));
  Player_Move player_move_1 (.in_1(button_2_out), .in_2(button_1_out), ._0(player_move_1__0), ._1(player_move_1__1));
  Counter #(.width(32), .max('h1f)) counter_1 (
    .load(button_1_out), .Q(counter_1_q), .clk(or_1_out));  // open: D, count, carry, clr
  or or_1 (or_1_out, button_1_out, button_2_out);
  // Probe on counter_1_q
  transpon transpon_1 (
    .in_1(player_move_1__0), .in_2(player_move_1__1), .in_3(player_move_1__1), .in_4(player_move_1__1),
    .in_5(player_move_1__1), ._0(transpon_1__0), ._1(transpon_1__1), ._2(transpon_1__2), ._3(transpon_1__3),
    ._4(transpon_1__4), ._5(transpon_1__5), ._6(transpon_1__6), ._7(transpon_1__7), ._8(transpon_1__8),
    ._9(transpon_1__9), ._10(transpon_1__10), ._11(transpon_1__11), ._12(transpon_1__12),
    ._13(transpon_1__13), ._14(transpon_1__14), ._15(transpon_1__15), ._16(transpon_1__16),
    ._17(transpon_1__17), ._18(transpon_1__18), ._19(transpon_1__19), ._20(transpon_1__20),
    ._21(transpon_1__21), ._22(transpon_1__22), ._23(transpon_1__23), ._24(transpon_1__24),
    ._25(transpon_1__25), ._26(transpon_1__26), ._27(transpon_1__27), ._28(transpon_1__28),
    ._29(transpon_1__29), ._30(transpon_1__30), ._31(transpon_1__31));  // open: in_6, in_7, in_8, in_9, in_10, in_11, in_12, in_13, in_14, in_15, in_16, in_17, in_18, in_19, in_20, in_21, in_22, in_23, in_24, in_25, in_26, in_27, in_28, in_29, in_30, in_31, in_32
  DotMatrix #(.inputtype("row"), .matrixcols(32), .matrixrows(32)) dotmatrix_2 (
    .row0(transpon_1__31), .row1(transpon_1__30), .row2(transpon_1__29), .row3(transpon_1__28),
    .row4(transpon_1__27), .row5(transpon_1__26), .row6(transpon_1__25), .row7(transpon_1__24),
    .row8(transpon_1__23), .row9(transpon_1__22), .row10(transpon_1__21), .row11(transpon_1__20),
    .row12(transpon_1__19), .row13(transpon_1__18), .row14(transpon_1__17), .row15(transpon_1__16),
    .row16(transpon_1__15), .row17(transpon_1__14), .row18(transpon_1__13), .row19(transpon_1__12),
    .row20(transpon_1__11), .row21(transpon_1__10), .row22(transpon_1__9), .row23(transpon_1__8),
    .row24(transpon_1__7), .row25(transpon_1__6), .row26(transpon_1__5), .row27(transpon_1__4),
    .row28(transpon_1__3), .row29(transpon_1__2), .row30(transpon_1__1), .row31(transpon_1__0));
endmodule

module \Перевернуть  (
  input  [31:0] in_1,
  output [31:0] out_2
);


  assign out_2 = {in_1[0], in_1[1], in_1[2], in_1[3], in_1[4], in_1[5], in_1[6], in_1[7], in_1[8], in_1[9], in_1[10], in_1[11], in_1[12], in_1[13], in_1[14], in_1[15], in_1[16], in_1[17], in_1[18], in_1[19], in_1[20], in_1[21], in_1[22], in_1[23], in_1[24], in_1[25], in_1[26], in_1[27], in_1[28], in_1[29], in_1[30], in_1[31]};
endmodule

module transpon (
  input  [31:0] in_1,
  input  [31:0] in_2,
  input  [31:0] in_3,
  input  [31:0] in_4,
  input  [31:0] in_5,
  input  [31:0] in_6,
  input  [31:0] in_7,
  input  [31:0] in_8,
  input  [31:0] in_9,
  input  [31:0] in_10,
  input  [31:0] in_11,
  input  [31:0] in_12,
  input  [31:0] in_13,
  input  [31:0] in_14,
  input  [31:0] in_15,
  input  [31:0] in_16,
  input  [31:0] in_17,
  input  [31:0] in_18,
  input  [31:0] in_19,
  input  [31:0] in_20,
  input  [31:0] in_21,
  input  [31:0] in_22,
  input  [31:0] in_23,
  input  [31:0] in_24,
  input  [31:0] in_25,
  input  [31:0] in_26,
  input  [31:0] in_27,
  input  [31:0] in_28,
  input  [31:0] in_29,
  input  [31:0] in_30,
  input  [31:0] in_31,
  input  [31:0] in_32,
  output [31:0] _0,
  output [31:0] _1,
  output [31:0] _2,
  output [31:0] _3,
  output [31:0] _4,
  output [31:0] _5,
  output [31:0] _6,
  output [31:0] _7,
  output [31:0] _8,
  output [31:0] _9,
  output [31:0] _10,
  output [31:0] _11,
  output [31:0] _12,
  output [31:0] _13,
  output [31:0] _14,
  output [31:0] _15,
  output [31:0] _16,
  output [31:0] _17,
  output [31:0] _18,
  output [31:0] _19,
  output [31:0] _20,
  output [31:0] _21,
  output [31:0] _22,
  output [31:0] _23,
  output [31:0] _24,
  output [31:0] _25,
  output [31:0] _26,
  output [31:0] _27,
  output [31:0] _28,
  output [31:0] _29,
  output [31:0] _30,
  output [31:0] _31
);

  \Перевернуть  \u_перевернуть_1  (
    .in_1({in_32[0], in_31[0], in_30[0], in_29[0], in_28[0], in_27[0], in_26[0], in_25[0], in_24[0], in_23[0], in_22[0], in_21[0], in_20[0], in_19[0], in_18[0], in_17[0], in_16[0], in_15[0], in_14[0], in_13[0], in_12[0], in_11[0], in_10[0], in_9[0], in_8[0], in_7[0], in_6[0], in_5[0], in_4[0], in_3[0], in_2[0], in_1[0]}),
    .out_2(_0));
  \Перевернуть  \u_перевернуть_2  (
    .in_1({in_32[4], in_31[4], in_30[4], in_29[4], in_28[4], in_27[4], in_26[4], in_25[4], in_24[4], in_23[4], in_22[4], in_21[4], in_20[4], in_19[4], in_18[4], in_17[4], in_16[4], in_15[4], in_14[4], in_13[4], in_12[4], in_11[4], in_10[4], in_9[4], in_8[4], in_7[4], in_6[4], in_5[4], in_4[4], in_3[4], in_2[4], in_1[4]}),
    .out_2(_4));
  \Перевернуть  \u_перевернуть_3  (
    .in_1({in_32[8], in_31[8], in_30[8], in_29[8], in_28[8], in_27[8], in_26[8], in_25[8], in_24[8], in_23[8], in_22[8], in_21[8], in_20[8], in_19[8], in_18[8], in_17[8], in_16[8], in_15[8], in_14[8], in_13[8], in_12[8], in_11[8], in_10[8], in_9[8], in_8[8], in_7[8], in_6[8], in_5[8], in_4[8], in_3[8], in_2[8], in_1[8]}),
    .out_2(_8));
  \Перевернуть  \u_перевернуть_4  (
    .in_1({in_32[12], in_31[12], in_30[12], in_29[12], in_28[12], in_27[12], in_26[12], in_25[12], in_24[12], in_23[12], in_22[12], in_21[12], in_20[12], in_19[12], in_18[12], in_17[12], in_16[12], in_15[12], in_14[12], in_13[12], in_12[12], in_11[12], in_10[12], in_9[12], in_8[12], in_7[12], in_6[12], in_5[12], in_4[12], in_3[12], in_2[12], in_1[12]}),
    .out_2(_12));
  \Перевернуть  \u_перевернуть_5  (
    .in_1({in_32[16], in_31[16], in_30[16], in_29[16], in_28[16], in_27[16], in_26[16], in_25[16], in_24[16], in_23[16], in_22[16], in_21[16], in_20[16], in_19[16], in_18[16], in_17[16], in_16[16], in_15[16], in_14[16], in_13[16], in_12[16], in_11[16], in_10[16], in_9[16], in_8[16], in_7[16], in_6[16], in_5[16], in_4[16], in_3[16], in_2[16], in_1[16]}),
    .out_2(_16));
  \Перевернуть  \u_перевернуть_6  (
    .in_1({in_32[20], in_31[20], in_30[20], in_29[20], in_28[20], in_27[20], in_26[20], in_25[20], in_24[20], in_23[20], in_22[20], in_21[20], in_20[20], in_19[20], in_18[20], in_17[20], in_16[20], in_15[20], in_14[20], in_13[20], in_12[20], in_11[20], in_10[20], in_9[20], in_8[20], in_7[20], in_6[20], in_5[20], in_4[20], in_3[20], in_2[20], in_1[20]}),
    .out_2(_20));
  \Перевернуть  \u_перевернуть_7  (
    .in_1({in_32[24], in_31[24], in_30[24], in_29[24], in_28[24], in_27[24], in_26[24], in_25[24], in_24[24], in_23[24], in_22[24], in_21[24], in_20[24], in_19[24], in_18[24], in_17[24], in_16[24], in_15[24], in_14[24], in_13[24], in_12[24], in_11[24], in_10[24], in_9[24], in_8[24], in_7[24], in_6[24], in_5[24], in_4[24], in_3[24], in_2[24], in_1[24]}),
    .out_2(_24));
  \Перевернуть  \u_перевернуть_8  (
    .in_1({in_32[28], in_31[28], in_30[28], in_29[28], in_28[28], in_27[28], in_26[28], in_25[28], in_24[28], in_23[28], in_22[28], in_21[28], in_20[28], in_19[28], in_18[28], in_17[28], in_16[28], in_15[28], in_14[28], in_13[28], in_12[28], in_11[28], in_10[28], in_9[28], in_8[28], in_7[28], in_6[28], in_5[28], in_4[28], in_3[28], in_2[28], in_1[28]}),
    .out_2(_28));
  \Перевернуть  \u_перевернуть_9  (
    .in_1({in_32[1], in_31[1], in_30[1], in_29[1], in_28[1], in_27[1], in_26[1], in_25[1], in_24[1], in_23[1], in_22[1], in_21[1], in_20[1], in_19[1], in_18[1], in_17[1], in_16[1], in_15[1], in_14[1], in_13[1], in_12[1], in_11[1], in_10[1], in_9[1], in_8[1], in_7[1], in_6[1], in_5[1], in_4[1], in_3[1], in_2[1], in_1[1]}),
    .out_2(_1));
  \Перевернуть  \u_перевернуть_10  (
    .in_1({in_32[5], in_31[5], in_30[5], in_29[5], in_28[5], in_27[5], in_26[5], in_25[5], in_24[5], in_23[5], in_22[5], in_21[5], in_20[5], in_19[5], in_18[5], in_17[5], in_16[5], in_15[5], in_14[5], in_13[5], in_12[5], in_11[5], in_10[5], in_9[5], in_8[5], in_7[5], in_6[5], in_5[5], in_4[5], in_3[5], in_2[5], in_1[5]}),
    .out_2(_5));
  \Перевернуть  \u_перевернуть_11  (
    .in_1({in_32[9], in_31[9], in_30[9], in_29[9], in_28[9], in_27[9], in_26[9], in_25[9], in_24[9], in_23[9], in_22[9], in_21[9], in_20[9], in_19[9], in_18[9], in_17[9], in_16[9], in_15[9], in_14[9], in_13[9], in_12[9], in_11[9], in_10[9], in_9[9], in_8[9], in_7[9], in_6[9], in_5[9], in_4[9], in_3[9], in_2[9], in_1[9]}),
    .out_2(_9));
  \Перевернуть  \u_перевернуть_12  (
    .in_1({in_32[13], in_31[13], in_30[13], in_29[13], in_28[13], in_27[13], in_26[13], in_25[13], in_24[13], in_23[13], in_22[13], in_21[13], in_20[13], in_19[13], in_18[13], in_17[13], in_16[13], in_15[13], in_14[13], in_13[13], in_12[13], in_11[13], in_10[13], in_9[13], in_8[13], in_7[13], in_6[13], in_5[13], in_4[13], in_3[13], in_2[13], in_1[13]}),
    .out_2(_13));
  \Перевернуть  \u_перевернуть_13  (
    .in_1({in_32[17], in_31[17], in_30[17], in_29[17], in_28[17], in_27[17], in_26[17], in_25[17], in_24[17], in_23[17], in_22[17], in_21[17], in_20[17], in_19[17], in_18[17], in_17[17], in_16[17], in_15[17], in_14[17], in_13[17], in_12[17], in_11[17], in_10[17], in_9[17], in_8[17], in_7[17], in_6[17], in_5[17], in_4[17], in_3[17], in_2[17], in_1[17]}),
    .out_2(_17));
  \Перевернуть  \u_перевернуть_14  (
    .in_1({in_32[21], in_31[21], in_30[21], in_29[21], in_28[21], in_27[21], in_26[21], in_25[21], in_24[21], in_23[21], in_22[21], in_21[21], in_20[21], in_19[21], in_18[21], in_17[21], in_16[21], in_15[21], in_14[21], in_13[21], in_12[21], in_11[21], in_10[21], in_9[21], in_8[21], in_7[21], in_6[21], in_5[21], in_4[21], in_3[21], in_2[21], in_1[21]}),
    .out_2(_21));
  \Перевернуть  \u_перевернуть_15  (
    .in_1({in_32[25], in_31[25], in_30[25], in_29[25], in_28[25], in_27[25], in_26[25], in_25[25], in_24[25], in_23[25], in_22[25], in_21[25], in_20[25], in_19[25], in_18[25], in_17[25], in_16[25], in_15[25], in_14[25], in_13[25], in_12[25], in_11[25], in_10[25], in_9[25], in_8[25], in_7[25], in_6[25], in_5[25], in_4[25], in_3[25], in_2[25], in_1[25]}),
    .out_2(_25));
  \Перевернуть  \u_перевернуть_16  (
    .in_1({in_32[29], in_31[29], in_30[29], in_29[29], in_28[29], in_27[29], in_26[29], in_25[29], in_24[29], in_23[29], in_22[29], in_21[29], in_20[29], in_19[29], in_18[29], in_17[29], in_16[29], in_15[29], in_14[29], in_13[29], in_12[29], in_11[29], in_10[29], in_9[29], in_8[29], in_7[29], in_6[29], in_5[29], in_4[29], in_3[29], in_2[29], in_1[29]}),
    .out_2(_29));
  \Перевернуть  \u_перевернуть_17  (
    .in_1({in_32[2], in_31[2], in_30[2], in_29[2], in_28[2], in_27[2], in_26[2], in_25[2], in_24[2], in_23[2], in_22[2], in_21[2], in_20[2], in_19[2], in_18[2], in_17[2], in_16[2], in_15[2], in_14[2], in_13[2], in_12[2], in_11[2], in_10[2], in_9[2], in_8[2], in_7[2], in_6[2], in_5[2], in_4[2], in_3[2], in_2[2], in_1[2]}),
    .out_2(_2));
  \Перевернуть  \u_перевернуть_18  (
    .in_1({in_32[6], in_31[6], in_30[6], in_29[6], in_28[6], in_27[6], in_26[6], in_25[6], in_24[6], in_23[6], in_22[6], in_21[6], in_20[6], in_19[6], in_18[6], in_17[6], in_16[6], in_15[6], in_14[6], in_13[6], in_12[6], in_11[6], in_10[6], in_9[6], in_8[6], in_7[6], in_6[6], in_5[6], in_4[6], in_3[6], in_2[6], in_1[6]}),
    .out_2(_6));
  \Перевернуть  \u_перевернуть_19  (
    .in_1({in_32[10], in_31[10], in_30[10], in_29[10], in_28[10], in_27[10], in_26[10], in_25[10], in_24[10], in_23[10], in_22[10], in_21[10], in_20[10], in_19[10], in_18[10], in_17[10], in_16[10], in_15[10], in_14[10], in_13[10], in_12[10], in_11[10], in_10[10], in_9[10], in_8[10], in_7[10], in_6[10], in_5[10], in_4[10], in_3[10], in_2[10], in_1[10]}),
    .out_2(_10));
  \Перевернуть  \u_перевернуть_20  (
    .in_1({in_32[14], in_31[14], in_30[14], in_29[14], in_28[14], in_27[14], in_26[14], in_25[14], in_24[14], in_23[14], in_22[14], in_21[14], in_20[14], in_19[14], in_18[14], in_17[14], in_16[14], in_15[14], in_14[14], in_13[14], in_12[14], in_11[14], in_10[14], in_9[14], in_8[14], in_7[14], in_6[14], in_5[14], in_4[14], in_3[14], in_2[14], in_1[14]}),
    .out_2(_14));
  \Перевернуть  \u_перевернуть_21  (
    .in_1({in_32[18], in_31[18], in_30[18], in_29[18], in_28[18], in_27[18], in_26[18], in_25[18], in_24[18], in_23[18], in_22[18], in_21[18], in_20[18], in_19[18], in_18[18], in_17[18], in_16[18], in_15[18], in_14[18], in_13[18], in_12[18], in_11[18], in_10[18], in_9[18], in_8[18], in_7[18], in_6[18], in_5[18], in_4[18], in_3[18], in_2[18], in_1[18]}),
    .out_2(_18));
  \Перевернуть  \u_перевернуть_22  (
    .in_1({in_32[22], in_31[22], in_30[22], in_29[22], in_28[22], in_27[22], in_26[22], in_25[22], in_24[22], in_23[22], in_22[22], in_21[22], in_20[22], in_19[22], in_18[22], in_17[22], in_16[22], in_15[22], in_14[22], in_13[22], in_12[22], in_11[22], in_10[22], in_9[22], in_8[22], in_7[22], in_6[22], in_5[22], in_4[22], in_3[22], in_2[22], in_1[22]}),
    .out_2(_22));
  \Перевернуть  \u_перевернуть_23  (
    .in_1({in_32[26], in_31[26], in_30[26], in_29[26], in_28[26], in_27[26], in_26[26], in_25[26], in_24[26], in_23[26], in_22[26], in_21[26], in_20[26], in_19[26], in_18[26], in_17[26], in_16[26], in_15[26], in_14[26], in_13[26], in_12[26], in_11[26], in_10[26], in_9[26], in_8[26], in_7[26], in_6[26], in_5[26], in_4[26], in_3[26], in_2[26], in_1[26]}),
    .out_2(_26));
  \Перевернуть  \u_перевернуть_24  (
    .in_1({in_32[30], in_31[30], in_30[30], in_29[30], in_28[30], in_27[30], in_26[30], in_25[30], in_24[30], in_23[30], in_22[30], in_21[30], in_20[30], in_19[30], in_18[30], in_17[30], in_16[30], in_15[30], in_14[30], in_13[30], in_12[30], in_11[30], in_10[30], in_9[30], in_8[30], in_7[30], in_6[30], in_5[30], in_4[30], in_3[30], in_2[30], in_1[30]}),
    .out_2(_30));
  \Перевернуть  \u_перевернуть_25  (
    .in_1({in_32[3], in_31[3], in_30[3], in_29[3], in_28[3], in_27[3], in_26[3], in_25[3], in_24[3], in_23[3], in_22[3], in_21[3], in_20[3], in_19[3], in_18[3], in_17[3], in_16[3], in_15[3], in_14[3], in_13[3], in_12[3], in_11[3], in_10[3], in_9[3], in_8[3], in_7[3], in_6[3], in_5[3], in_4[3], in_3[3], in_2[3], in_1[3]}),
    .out_2(_3));
  \Перевернуть  \u_перевернуть_26  (
    .in_1({in_32[7], in_31[7], in_30[7], in_29[7], in_28[7], in_27[7], in_26[7], in_25[7], in_24[7], in_23[7], in_22[7], in_21[7], in_20[7], in_19[7], in_18[7], in_17[7], in_16[7], in_15[7], in_14[7], in_13[7], in_12[7], in_11[7], in_10[7], in_9[7], in_8[7], in_7[7], in_6[7], in_5[7], in_4[7], in_3[7], in_2[7], in_1[7]}),
    .out_2(_7));
  \Перевернуть  \u_перевернуть_27  (
    .in_1({in_32[11], in_31[11], in_30[11], in_29[11], in_28[11], in_27[11], in_26[11], in_25[11], in_24[11], in_23[11], in_22[11], in_21[11], in_20[11], in_19[11], in_18[11], in_17[11], in_16[11], in_15[11], in_14[11], in_13[11], in_12[11], in_11[11], in_10[11], in_9[11], in_8[11], in_7[11], in_6[11], in_5[11], in_4[11], in_3[11], in_2[11], in_1[11]}),
    .out_2(_11));
  \Перевернуть  \u_перевернуть_28  (
    .in_1({in_32[15], in_31[15], in_30[15], in_29[15], in_28[15], in_27[15], in_26[15], in_25[15], in_24[15], in_23[15], in_22[15], in_21[15], in_20[15], in_19[15], in_18[15], in_17[15], in_16[15], in_15[15], in_14[15], in_13[15], in_12[15], in_11[15], in_10[15], in_9[15], in_8[15], in_7[15], in_6[15], in_5[15], in_4[15], in_3[15], in_2[15], in_1[15]}),
    .out_2(_15));
  \Перевернуть  \u_перевернуть_29  (
    .in_1({in_32[19], in_31[19], in_30[19], in_29[19], in_28[19], in_27[19], in_26[19], in_25[19], in_24[19], in_23[19], in_22[19], in_21[19], in_20[19], in_19[19], in_18[19], in_17[19], in_16[19], in_15[19], in_14[19], in_13[19], in_12[19], in_11[19], in_10[19], in_9[19], in_8[19], in_7[19], in_6[19], in_5[19], in_4[19], in_3[19], in_2[19], in_1[19]}),
    .out_2(_19));
  \Перевернуть  \u_перевернуть_30  (
    .in_1({in_32[23], in_31[23], in_30[23], in_29[23], in_28[23], in_27[23], in_26[23], in_25[23], in_24[23], in_23[23], in_22[23], in_21[23], in_20[23], in_19[23], in_18[23], in_17[23], in_16[23], in_15[23], in_14[23], in_13[23], in_12[23], in_11[23], in_10[23], in_9[23], in_8[23], in_7[23], in_6[23], in_5[23], in_4[23], in_3[23], in_2[23], in_1[23]}),
    .out_2(_23));
  \Перевернуть  \u_перевернуть_31  (
    .in_1({in_32[27], in_31[27], in_30[27], in_29[27], in_28[27], in_27[27], in_26[27], in_25[27], in_24[27], in_23[27], in_22[27], in_21[27], in_20[27], in_19[27], in_18[27], in_17[27], in_16[27], in_15[27], in_14[27], in_13[27], in_12[27], in_11[27], in_10[27], in_9[27], in_8[27], in_7[27], in_6[27], in_5[27], in_4[27], in_3[27], in_2[27], in_1[27]}),
    .out_2(_27));
  \Перевернуть  \u_перевернуть_32  (
    .in_1({in_32[31], in_31[31], in_30[31], in_29[31], in_28[31], in_27[31], in_26[31], in_25[31], in_24[31], in_23[31], in_22[31], in_21[31], in_20[31], in_19[31], in_18[31], in_17[31], in_16[31], in_15[31], in_14[31], in_13[31], in_12[31], in_11[31], in_10[31], in_9[31], in_8[31], in_7[31], in_6[31], in_5[31], in_4[31], in_3[31], in_2[31], in_1[31]}),
    .out_2(_31));

  // Other names for the same wires on the sheet: _0_t[31:0] = in_1; _1_t[31:0] = in_2; _2_t[31:0] = in_3;
  //   _3_t[31:0] = in_4; _4_t[31:0] = in_5; _5_t[31:0] = in_6; _6_t[31:0] = in_7; _7_t[31:0] = in_8;
  //   _8_t[31:0] = in_9; _9_t[31:0] = in_10; _10_t[31:0] = in_11; _11_t[31:0] = in_12; _12_t[31:0] = in_13;
  //   _13_t[31:0] = in_14; _14_t[31:0] = in_15; _15_t[31:0] = in_16; _16_t[31:0] = in_17; _17_t[31:0] = in_18;
  //   _18_t[31:0] = in_19; _19_t[31:0] = in_20; _20_t[31:0] = in_21; _21_t[31:0] = in_22; _22_t[31:0] = in_23;
  //   _23_t[31:0] = in_24; _24_t[31:0] = in_25; _25_t[31:0] = in_26; _26_t[31:0] = in_27; _27_t[31:0] = in_28;
  //   _28_t[31:0] = in_29; _29_t[31:0] = in_30; _30_t[31:0] = in_31; _31_t[31:0] = in_32
endmodule
